# Fritzing sketch blink_illuminated_pushbutton (saved by Fritzing 0.9.4)
breadboards: 1

parts:
  Part1 = Arduino Mega 2560 (Rev3)
  LED1 = LEDs [package=led10mm]
  R1 = Resistor [tolerance=±5% resistance=220 package="2512 [SMD]"]
  R2 = Resistor [tolerance=±5% resistance=220 package="2512 [SMD]"]
  R3 = Resistor [tolerance=±5% resistance=10k package=THT]
  S1 = Round Pushbutton
  LED2 = LEDs [package=led10mm]

nets:
  N1: Part1.D21/SCL, R2.Pin_0
  N2: Part1.D20/SDA, R3.Pin_0, S1.leg1
  N3: Part1.GND, R2.Pin_1, R3.Pin_1, LED2.C, LED2.A
  N4: Part1.5V, LED1.C, S1.leg0
  N5: Part1.D25, R1.Pin_1
  N6: LED1.A, R1.Pin_0

notes:
  Pushbutton is illuminated. LED pin is mocked, the red and blue wire are connected to + and - on the pushbutton.
